# Fritzing sketch 20171201_Nano_Temperature_Display-MAX31855 (saved by Fritzing 0.9.3b)
breadboards: 3

parts:
  Part1 = Arduino Nano (Rev3.0)
  Part2 = Adafruit Thermocouple Amplifier MAX31855 [part_number="Adafruit #269"]
  DHT1 = DHT22 Humidity and Temperature Sensor
  R1 = Resistor [tolerance=±5% resistance=10k package=THT]
  U2 = LCD-16X2 [package=lcd-16x2_nosilk]
  R5 = Trimmer Potentiometer [maximum_resistance=10kΩ package=THT]
  R6 = Resistor [tolerance=±1% resistance=220 package=THT]

nets:
  GND: Part1.GND, Part2.GND, DHT1.GND, U2.VSS, U2.R_W, U2.K, R5.leg2
  N1: Part1.D2, U2.DB7
  N2: Part1.D3, U2.DB6
  N3: Part1.D4, U2.DB5
  N4: Part1.D5, U2.DB4
  N5: Part1.D6, DHT1.DATA, R1.Pin_1
  N6: Part1.D7, Part2.DO
  N7: Part1.D8, Part2.CS
  N8: Part1.D9, Part2.CLK
  N9: Part1.D11/MOSI, U2.E
  N10: Part1.D12/MISO, U2.RS
  VDD: Part1.5V, Part2.VIN, DHT1.VDD, R1.Pin_0, U2.VDD, R5.leg1, R6.Pin_0
  N11: U2.VO, R5.wiper
  N12: U2.A, R6.Pin_1

notes:
  Pins:
  (5V)(Dat)(None)(GND)
  Banggood 20X4 Display

custom parts:
  Adafruit Thermocouple Amplifier MAX31855: Thermocouples are very sensitive, requiring a good amplifier with a cold-compensation reference. The MAX31855K does everything for you, and can be easily interfaced with any microcontroller, even one without an analog input. This breakout board has the chip itself, a 3.3V regulator with 10uF bypass capacitors and level shifting circuitry, all assembled and tested. Comes with a 2 pin terminal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
