# Fritzing sketch 20171222_Nano_Temperature_Display-IsolatedMAX31855 (saved by Fritzing 0.9.3b)
circuit board: 10cm x 6cm
breadboards: 3
perfboards: 1

parts:
  Part3 = Arduino Nano (Rev3.0)
  DHT2 = DHT22 Humidity and Temperature Sensor
  R7 = Resistor [tolerance=±5% resistance=10k package=THT]
  U3 = LCD-16X2 [package=lcd-16x2_nosilk]
  R8 = Trimmer Potentiometer [maximum_resistance=10kΩ package=THT]
  R9 = Resistor [tolerance=±1% resistance=220 package=THT]
  Part5 = Adafruit Thermocouple Amplifier MAX31855 [part_number="Adafruit #269"]
  IC2 = ADuM5401 [chip_label=ADuM5401 package="DIP (Dual Inline) [THT]"]
  SN74AHC1G1 = SN74AHC1G125 3 state buffer [package="DIP (Dual Inline) [THT]"]
  R10 = Resistor [tolerance=±1% resistance=15k package=THT]  # not connected

nets:
  GND: Part3.GND, DHT2.GND, U3.VSS, U3.R_W, U3.K, R8.leg2, IC2.GND1, SN74AHC1G1.GND
  N1: Part3.D2, U3.DB7
  N2: Part3.D3, U3.DB6
  N3: Part3.D4, U3.DB5
  N4: Part3.D5, U3.DB4
  N5: Part3.D6, DHT2.DATA, R7.Pin_1
  N6: Part3.D7, SN74AHC1G1.Y
  N7: Part3.D8, IC2.Via, SN74AHC1G1.OE
  N8: Part3.D9, IC2.Vib
  N9: Part3.D11/MOSI, U3.E
  N10: Part3.D12/MISO, U3.RS
  VDD: Part3.5V, DHT2.VDD, R7.Pin_0, U3.VDD, R8.leg1, R9.Pin_0, IC2.Vin, SN74AHC1G1.VCC
  N11: U3.VO, R8.wiper
  N12: U3.A, R9.Pin_1
  N13: Part5.VIN, IC2.Vsel, IC2.Viso
  N14: Part5.GND, IC2.GNDiso
  N15: Part5.DO, IC2.Vid
  N16: Part5.CS, IC2.Voa
  N17: Part5.CLK, IC2.Vob
  N18: IC2.Vod, SN74AHC1G1.A

notes:
  Pins:
  (5V)(Dat)(None)(GND)
  Banggood 20X4 Display

custom parts:
  Adafruit Thermocouple Amplifier MAX31855: Thermocouples are very sensitive, requiring a good amplifier with a cold-compensation reference. The MAX31855K does everything for you, and can be easily interfaced with any microcontroller, even one without an analog input. This breakout board has the chip itself, a 3.3V regulator with 10uF bypass capacitors and level shifting circuitry, all assembled and tested. Comes with a 2 pin terminal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
  ADuM5401: Quad-Channel, 2.5 kV Isolators with Integrated DC-to-DC Converter
  SN74AHC1G125 3 state buffer: A DIP stand-in part for whatever IC you want. With 6 pins on a 300mil dual inline package (DIP) footprint.
